// Logisim project Final_project.circ as structural Verilog: 8 circuits, main circuit main
module FullAdder (
  input  A,
  input  B,
  input  Cin,
  output Sum,
  output Cout
);

  wire and_1_out, and_2_out, xor_1_out;

  xor xor_1 (xor_1_out, A, B);
  and and_1 (and_1_out, Cin, xor_1_out);
  xor xor_2 (Sum, xor_1_out, Cin);
  and and_2 (and_2_out, A, B);
  or or_1 (Cout, and_1_out, and_2_out);

  // Notes on the sheet:
  //   1-Bit Full Adder Module
  //   We have used this 1-bit Full adder on the main simulator to simulate adder, subtractor and comparator 
endmodule

// Splitter
module main (
  input  in_1,
  input  in_2,
  input  Mode_M_0_Add_1_Sub_93f06aea,
  input  in_4,
  output [3:0] out_5,
  output [3:0] out_6,
  output [3:0] out_7,
  output out_8,
  output [3:0] Output_S,
  output [3:0] out_10,
  output Carry_Out
);

  wire dipswitch_1_sw1, dipswitch_1_sw2, dipswitch_1_sw3, dipswitch_1_sw4, dipswitch_1_sw5, dipswitch_1_sw6,
       dipswitch_1_sw7, dipswitch_1_sw8, dipswitch_1_sw9, dipswitch_2_sw1, dipswitch_2_sw2, dipswitch_2_sw3,
       dipswitch_2_sw4, dipswitch_2_sw5, dipswitch_2_sw6, dipswitch_2_sw7, dipswitch_2_sw8, dipswitch_2_sw9,
       fulladder_1_cout, fulladder_2_cout, fulladder_3_cout, negative_comparator_1_gto,
       negative_comparator_1_lto, nor_1_out, nor_2_out, unsigned_comparaotr_1_equal,
       unsigned_comparaotr_1_greater, unsigned_comparaotr_1_samller, xor_1_out, xor_2_out, xor_3_out,
       xor_4_out, xor_5_out;
  wire [3:0] key_pad_converte_2_final;

  DipSwitch #(.number(9)) dipswitch_1 (
    .sw1(dipswitch_1_sw1), .sw2(dipswitch_1_sw2), .sw3(dipswitch_1_sw3), .sw4(dipswitch_1_sw4),
    .sw5(dipswitch_1_sw5), .sw6(dipswitch_1_sw6), .sw7(dipswitch_1_sw7), .sw8(dipswitch_1_sw8),
    .sw9(dipswitch_1_sw9));
  DipSwitch #(.number(9)) dipswitch_2 (
    .sw1(dipswitch_2_sw1), .sw2(dipswitch_2_sw2), .sw3(dipswitch_2_sw3), .sw4(dipswitch_2_sw4),
    .sw5(dipswitch_2_sw5), .sw6(dipswitch_2_sw6), .sw7(dipswitch_2_sw7), .sw8(dipswitch_2_sw8),
    .sw9(dipswitch_2_sw9));
  Key_pad_converte key_pad_converte_1 (
    .D1(dipswitch_1_sw1), .D2(dipswitch_1_sw2), .D3(dipswitch_1_sw3), .D4(dipswitch_1_sw4),
    .D5(dipswitch_1_sw5), .D6(dipswitch_1_sw6), .D7(dipswitch_1_sw7), .D8(dipswitch_1_sw8), .sign(in_1),
    .D9(dipswitch_1_sw9), .\final (out_6));  // open: in_2, in_6, out_13, out_14, out_15, out_17, out_18
  Key_pad_converte key_pad_converte_2 (
    .D1(dipswitch_2_sw1), .D2(dipswitch_2_sw2), .D3(dipswitch_2_sw3), .D4(dipswitch_2_sw4),
    .D5(dipswitch_2_sw5), .D6(dipswitch_2_sw6), .D7(dipswitch_2_sw7), .D8(dipswitch_2_sw8), .sign(in_4),
    .D9(dipswitch_2_sw9), .\final (key_pad_converte_2_final));  // open: in_2, in_6, out_13, out_14, out_15, out_17, out_18
  xor xor_1 (xor_1_out, Mode_M_0_Add_1_Sub_93f06aea, key_pad_converte_2_final[0]);
  xor xor_2 (xor_2_out, Mode_M_0_Add_1_Sub_93f06aea, key_pad_converte_2_final[1]);
  xor xor_3 (xor_3_out, Mode_M_0_Add_1_Sub_93f06aea, key_pad_converte_2_final[2]);
  xor xor_4 (xor_4_out, key_pad_converte_2_final[3], Mode_M_0_Add_1_Sub_93f06aea);
  FullAdder fulladder_1 (
    .A(out_6[0]), .B(xor_1_out), .Cin(Mode_M_0_Add_1_Sub_93f06aea), .Sum(Output_S[0]), .Cout(fulladder_1_cout));
  FullAdder fulladder_2 (
    .A(out_6[1]), .B(xor_2_out), .Cin(fulladder_1_cout), .Sum(Output_S[1]), .Cout(fulladder_2_cout));
  FullAdder fulladder_3 (
    .A(out_6[2]), .B(xor_3_out), .Cin(fulladder_2_cout), .Sum(Output_S[2]), .Cout(fulladder_3_cout));
  FullAdder fulladder_4 (.A(out_6[3]), .B(xor_4_out), .Cin(fulladder_3_cout), .Sum(Output_S[3]), .Cout(Carry_Out));
  nor nor_1 (nor_1_out, Output_S[0], Output_S[1], Output_S[2], Output_S[3]);
  // AND_Gate and_1 has open pins: in0=Output_S[3], in1=Mode_M_0_Add_1_Sub_93f06aea, out=open
  // AND_Gate and_2 has open pins: in0=nor_1_out, in1=Mode_M_0_Add_1_Sub_93f06aea, out=open
  Unsigned_Comparaotr unsigned_comparaotr_1 (
    .A0(out_6[3]), .B0(key_pad_converte_2_final[3]), .A1(out_6[2]), .B1(key_pad_converte_2_final[2]),
    .A2(out_6[1]), .B2(key_pad_converte_2_final[1]), .A3(out_6[0]), .B3(key_pad_converte_2_final[0]),
    .greater(unsigned_comparaotr_1_greater), .equal(unsigned_comparaotr_1_equal),
    .samller(unsigned_comparaotr_1_samller));
  nor nor_2 (nor_2_out, nor_1_out, Output_S[3]);
  // AND_Gate and_3 has open pins: in0=nor_2_out, in1=Mode_M_0_Add_1_Sub_93f06aea, out=open
  Negative_comparator negative_comparator_1 (
    .A3(out_6[3]), .B3(key_pad_converte_2_final[3]), .LT(unsigned_comparaotr_1_samller),
    .GT(unsigned_comparaotr_1_greater), .LTO(negative_comparator_1_lto), .GTO(negative_comparator_1_gto));
  MUx mux_1 (
    .Sign_bit(Output_S[3]), .A1(Output_S[3]), .B1(out_10[0]), .A2(Output_S[2]), .B2(out_10[1]),
    .A3(Output_S[1]), .B3(out_10[2]), .A4(Output_S[0]), .B4(out_10[3]), .out_10(out_5));
  Complment_2 complment_2_1 (
    .IF1(1'b0), .IF2(1'b0), .IF3(1'b0), .IN1(Output_S[3]), .IN2(Output_S[2]), .IN3(Output_S[1]), .IF4(1'b1),
    .IN4(Output_S[0]), .OT1(in_2), .OT3(out_8), .OP1(out_10[0]), .OP4(out_10[3]), .OP2(out_10[1]),
    .OP3(out_10[2]));
  LED Less_than (.in(negative_comparator_1_lto));
  LED Greater_than (.in(negative_comparator_1_gto));
  LED Equal (.in(unsigned_comparaotr_1_equal));
  xor xor_5 (xor_5_out, fulladder_3_cout, Carry_Out);
  OVER over_1 (
    .Over_flow(xor_5_out), .IN1(out_5[3]), .E1(1'b1), .IN2(out_5[2]), .E2(1'b1), .IN3(out_5[1]), .E3(1'b1),
    .IN4(out_5[0]), .E4(1'b0), .out_10(out_7));
  LED Sign_led (.in(Output_S[3]));
  Hex_Digit_Display hex_digit_display_1 (.value(out_7));  // open: dp

  // Notes on the sheet:
  //   4-Bit Digital calculator Design Simulator
  //   Adder, Subtractor and Comparator
  //   Hex Digital Display
endmodule

module Complment_2 (
  input  IF1,
  input  IF2,
  input  IF3,
  input  IN1,
  input  IN2,
  input  IN3,
  input  IF4,
  input  IN4,
  input  OT1,
  output OT3,
  output OP1,
  output OP4,
  output OP2,
  output OP3
);

  wire and_1_out, and_2_out, and_3_out, and_4_out, and_5_out, and_6_out, and_7_out, and_8_out, not_1_out,
       not_2_out, not_3_out, not_4_out, xor_2_out, xor_4_out, xor_5_out, xor_7_out, xor_8_out, xor_10_out,
       xor_11_out;

  xor xor_1 (OT3, and_2_out, and_1_out);
  and and_1 (and_1_out, xor_2_out, xor_4_out);
  and and_2 (and_2_out, IF1, not_1_out);
  not not_1 (not_1_out, IN1);
  xor xor_2 (xor_2_out, not_1_out, IF1);
  xor xor_3 (OP1, xor_4_out, xor_2_out);
  xor xor_4 (xor_4_out, and_4_out, and_3_out);
  and and_3 (and_3_out, xor_5_out, xor_7_out);
  and and_4 (and_4_out, IF2, not_2_out);
  not not_2 (not_2_out, IN2);
  xor xor_5 (xor_5_out, not_2_out, IF2);
  xor xor_6 (OP2, xor_7_out, xor_5_out);
  xor xor_7 (xor_7_out, and_6_out, and_5_out);
  and and_5 (and_5_out, xor_8_out, xor_10_out);
  and and_6 (and_6_out, IF3, not_3_out);
  not not_3 (not_3_out, IN3);
  xor xor_8 (xor_8_out, not_3_out, IF3);
  xor xor_9 (OP3, xor_10_out, xor_8_out);
  xor xor_10 (xor_10_out, and_8_out, and_7_out);
  and and_7 (and_7_out, xor_11_out, OT1);
  and and_8 (and_8_out, IF4, not_4_out);
  not not_4 (not_4_out, IN4);
  xor xor_11 (xor_11_out, not_4_out, IF4);
  xor xor_12 (OP4, OT1, xor_11_out);
endmodule

module MUx (
  input  Sign_bit,
  input  A1,
  input  B1,
  input  A2,
  input  B2,
  input  A3,
  input  B3,
  input  A4,
  input  B4,
  output [3:0] out_10
);

  wire and_1_out, and_2_out, and_3_out, and_4_out, and_5_out, and_6_out, and_7_out, and_8_out, not_1_out;

  not not_1 (not_1_out, Sign_bit);
  and and_1 (and_1_out, A1, not_1_out);
  and and_2 (and_2_out, B1, Sign_bit);
  and and_3 (and_3_out, A2, not_1_out);
  and and_4 (and_4_out, B2, Sign_bit);
  and and_5 (and_5_out, A3, not_1_out);
  and and_6 (and_6_out, B3, Sign_bit);
  and and_7 (and_7_out, A4, not_1_out);
  and and_8 (and_8_out, B4, Sign_bit);
  or or_1 (out_10[3], and_1_out, and_2_out);
  or or_2 (out_10[2], and_3_out, and_4_out);
  or or_3 (out_10[1], and_5_out, and_6_out);
  or or_4 (out_10[0], and_7_out, and_8_out);
endmodule

module OVER (
  input  Over_flow,
  input  IN1,
  input  E1,
  input  IN2,
  input  E2,
  input  IN3,
  input  E3,
  input  IN4,
  input  E4,
  output [3:0] out_10
);

  wire and_1_out, and_2_out, and_3_out, and_4_out, and_5_out, and_6_out, and_7_out, and_8_out, not_1_out;

  not not_1 (not_1_out, Over_flow);
  and and_1 (and_1_out, IN1, not_1_out);
  and and_2 (and_2_out, E1, Over_flow);
  and and_3 (and_3_out, IN2, not_1_out);
  and and_4 (and_4_out, E2, Over_flow);
  and and_5 (and_5_out, IN3, not_1_out);
  and and_6 (and_6_out, E3, Over_flow);
  and and_7 (and_7_out, IN4, not_1_out);
  and and_8 (and_8_out, E4, Over_flow);
  or or_1 (out_10[3], and_1_out, and_2_out);
  or or_2 (out_10[2], and_3_out, and_4_out);
  or or_3 (out_10[1], and_5_out, and_6_out);
  or or_4 (out_10[0], and_7_out, and_8_out);
endmodule

module Negative_comparator (
  input  A3,
  input  B3,
  input  LT,
  input  GT,
  output LTO,
  output GTO
);

  wire and_1_out, and_2_out, and_3_out, and_4_out, and_5_out, and_6_out, not_1_out, not_2_out;

  not not_1 (not_1_out, B3);
  not not_2 (not_2_out, A3);
  and and_1 (and_1_out, A3, not_1_out);
  and and_2 (and_2_out, not_2_out, not_1_out, LT);
  and and_3 (and_3_out, A3, B3, GT);
  and and_4 (and_4_out, not_2_out, B3);
  and and_5 (and_5_out, not_2_out, not_1_out, GT);
  and and_6 (and_6_out, A3, B3, LT);
  or or_1 (LTO, and_1_out, and_2_out, and_3_out);
  or or_2 (GTO, and_4_out, and_5_out, and_6_out);
endmodule

module Unsigned_Comparaotr (
  input  A0,
  input  B0,
  input  A1,
  input  B1,
  input  A2,
  input  B2,
  input  A3,
  input  B3,
  output greater,
  output equal,
  output samller
);

  wire and_1_out, and_2_out, and_3_out, and_4_out, and_5_out, and_6_out, and_7_out, and_8_out, not_1_out,
       not_2_out, not_3_out, not_4_out, not_5_out, not_6_out, not_7_out, not_8_out, xnor_1_out, xnor_2_out,
       xnor_3_out, xnor_4_out;

  not not_1 (not_1_out, B0);
  not not_2 (not_2_out, B1);
  not not_3 (not_3_out, B2);
  not not_4 (not_4_out, B3);
  xnor xnor_1 (xnor_1_out, A0, B0);
  xnor xnor_2 (xnor_2_out, A1, B1);
  xnor xnor_3 (xnor_3_out, A2, B2);
  xnor xnor_4 (xnor_4_out, A3, B3);
  not not_5 (not_5_out, A3);
  not not_6 (not_6_out, A2);
  not not_7 (not_7_out, A1);
  not not_8 (not_8_out, A0);
  and and_1 (and_1_out, not_1_out, A0, xnor_2_out, xnor_3_out, xnor_4_out);
  and and_2 (and_2_out, not_2_out, A1, xnor_3_out, xnor_4_out);
  and and_3 (and_3_out, not_3_out, A2, xnor_4_out);
  and and_4 (and_4_out, not_4_out, A3);
  and and_5 (and_5_out, B3, not_5_out);
  and and_6 (and_6_out, xnor_4_out, B2, not_6_out);
  and and_7 (and_7_out, xnor_4_out, xnor_3_out, B1, not_7_out);
  and and_8 (and_8_out, xnor_4_out, xnor_3_out, xnor_2_out, not_8_out, B0);
  or or_1 (greater, and_1_out, and_2_out, and_3_out, and_4_out);
  and and_9 (equal, xnor_1_out, xnor_2_out, xnor_3_out, xnor_4_out);
  or or_2 (samller, and_5_out, and_6_out, and_7_out, and_8_out);
endmodule

module Key_pad_converte (
  input  D1,
  input  [3:0] in_2,
  input  D2,
  input  D3,
  input  D4,
  input  in_6,
  input  D5,
  input  D6,
  input  D7,
  input  D8,
  input  sign,
  input  D9,
  output out_13,
  output [3:0] out_14,
  output out_15,
  output [3:0] \final ,
  output out_17,
  output out_18
);

  or or_1 (out_13, D1, D3, D5, D7, D9);
  or or_2 (out_15, D3, D2, D6, D7);
  or or_3 (out_18, D8, D9);
  or or_4 (out_17, D4, D5, D6, D7);
  Complment_2 complment_2_1 (
    .IF1(in_2[3]), .IF2(in_2[2]), .IF3(in_2[1]), .IN1(out_18), .IN2(out_17), .IN3(out_15), .IF4(in_2[0]),
    .IN4(out_13), .OT1(in_6), .OP1(out_14[3]), .OP4(out_14[2]), .OP2(out_14[1]), .OP3(out_14[0]));  // open: OT3
  MUx mux_1 (
    .Sign_bit(sign), .A1(out_13), .B1(out_14[3]), .A2(out_15), .B2(out_14[2]), .A3(out_17), .B3(out_14[1]),
    .A4(out_18), .B4(out_14[0]), .out_10(\final ));
endmodule
